# Fritzing sketch e-11blaster (saved by Fritzing 0.9.2b)
breadboards: 1

parts:
  Trigger = Pushbutton [part_number=S1 package=THT]
  Mode = Pushbutton [part_number=S2 package=THT]
  Reload = Pushbutton [part_number=S3 package=THT]
  Arduino = Arduino Nano (Rev3.0) [part_number=AD1]
  V1 = DC Power [voltage=7.4V part_number=V1]
  R1 = Resistor [tolerance=±5% resistance=220 part_number=R1 package=THT]
  Power_Indicator = LED - 5mm [color="Red (633nm)" part_number=LED3 package="5 mm [THT]"]
  Grove_10_Segment_LED = female pin header, 4 pins [form="♀ (female)" part_number=LED1]
  Ada_Fruit_NeoPixel = female pin header, 3 pins [form="♀ (female)" part_number=LED2]
  R2 = Resistor [tolerance=±5% resistance=470 part_number=R2 package=THT]

nets:
  N1: Trigger.leg0, Mode.leg0, Reload.leg0, Arduino.GND, V1.V-, Power_Indicator.cathode, Grove_10_Segment_LED.pin1, Ada_Fruit_NeoPixel.pin3
  N2: Trigger.leg1, Arduino.D2
  N3: Mode.leg1, Arduino.D3
  N4: Reload.leg1, Arduino.D4
  N5: Arduino.D5, Grove_10_Segment_LED.pin4
  N6: Arduino.D6, Grove_10_Segment_LED.pin3
  N7: Arduino.D7, R2.Pin_0
  N8: Arduino.D11/MOSI, R1.Pin_0
  N9: Arduino.VIN, V1.V+
  N10: Arduino.5V, Grove_10_Segment_LED.pin2, Ada_Fruit_NeoPixel.pin1
  N11: R1.Pin_1, Power_Indicator.anode
  N12: Ada_Fruit_NeoPixel.pin2, R2.Pin_1

notes:
  https://github.com/themaninthesuitcase/e-11blaster
  Copyright © 2015 Chris Pearson. Available under MIT License.
